# Fritzing sketch Esquema (saved by Fritzing 0.9.3b)
breadboards: 2

parts:
  Componente1 = Arduino Uno (Rev3) - ICSP
  TIP122 = npn-Powertransistor [package="TO220 [THT]"]
  S1 = Pushbutton [package="[THT]"]
  S2 = Pushbutton [package="[THT]"]
  S3 = Pushbutton [package="[THT]"]
  U2 = POT [package=pot_alpha_rv16af-20]
  U3 = POT [package=alps_pot]
  M1 = DC Motor
  VCC1 = 4 x AAA Battery Mount
  R1 = Resistor [tolerance=±5% resistance=220 package="1206 [SMD]"]
  R2 = Resistor [tolerance=±5% resistance=220 package="1206 [SMD]"]
  R3 = Resistor [tolerance=±5% resistance=220 package="1206 [SMD]"]
  Kp<_Ki_Kd_Sp = LCD screen [part_number=asdasd]

nets:
  N1: Componente1.A0, U3.S
  N2: Componente1.D8, S3.Pin_1, S3.Pin_2
  N3: Componente1.D9_PWM, R1.Pin_0, R2.Pin_0
  N4: Componente1.D10_PWM/SS, S2.Pin_1, S2.Pin_2
  N5: Componente1.D11_PWM/MOSI, Kp<_Ki_Kd_Sp.E
  N6: Componente1.D12/MISO, Kp<_Ki_Kd_Sp.RS
  GND: Componente1.GND, TIP122.emitter, U2.E, U3.A, VCC1.-, R3.Pin_0, Kp<_Ki_Kd_Sp.VSS, Kp<_Ki_Kd_Sp.R/W, Kp<_Ki_Kd_Sp.LED-
  N7: Componente1.D2, Kp<_Ki_Kd_Sp.DB7
  N8: Componente1.D3_PWM, Kp<_Ki_Kd_Sp.DB6
  N9: Componente1.D4, Kp<_Ki_Kd_Sp.DB5
  N10: Componente1.D5_PWM, Kp<_Ki_Kd_Sp.DB4
  N11: Componente1.D7, S1.Pin_1, S1.Pin_2
  5V: Componente1.5V, U2.A, U3.E, Kp<_Ki_Kd_Sp.VDD, Kp<_Ki_Kd_Sp.LED+
  N12: TIP122.base, R1.Pin_1, R2.Pin_1
  N13: TIP122.collector, M1.pin_1
  N14: S1.Pin_3, S1.Pin_4, S2.Pin_3, S2.Pin_4, S3.Pin_3, S3.Pin_4, R3.Pin_1
  N15: U2.S, Kp<_Ki_Kd_Sp.V0
